// Logisim project scheme.circ as structural Verilog: 1 circuit, main circuit main
module main (
  input  x2,
  input  x1,
  input  x0,
  input  in_4,
  output y1,
  output y0
);

  wire and_1_out, and_2_out, and_3_out, and_4_out, and_5_out, and_6_out, and_7_out, and_8_out, and_9_out,
       and_10_out, and_11_out, and_12_out, and_13_out, and_14_out, and_15_out, and_16_out, and_17_out,
       and_18_out, and_19_out, and_20_out, and_21_out, and_22_out, and_23_out, and_24_out, and_25_out, D0_q,
       D1_q, D2_q, not_1_out, not_2_out, not_3_out, not_4_out, not_5_out, not_6_out, not_7_out, not_8_out,
       not_9_out, not_10_out, not_11_out, not_12_out, not_13_out, not_14_out, not_15_out, not_16_out,
       not_17_out, not_18_out, not_19_out, not_20_out, not_21_out, not_22_out, not_23_out, not_24_out,
       not_25_out, not_26_out, not_27_out, not_28_out, not_29_out, not_30_out, not_31_out, not_32_out,
       not_33_out, not_34_out, not_35_out, not_36_out, not_37_out, not_38_out, not_39_out, not_40_out,
       not_41_out, not_42_out, not_43_out, not_44_out, not_45_out, or_3_out, or_4_out, or_5_out;

  not not_1 (not_1_out, x2);
  not not_2 (not_2_out, x0);
  not not_3 (not_3_out, x2);
  not not_4 (not_4_out, x0);
  not not_5 (not_5_out, x1);
  not not_6 (not_6_out, D2_q);
  not not_7 (not_7_out, D1_q);
  not not_8 (not_8_out, D0_q);
  not not_9 (not_9_out, x0);
  not not_10 (not_10_out, D2_q);
  not not_11 (not_11_out, D2_q);
  not not_12 (not_12_out, D1_q);
  not not_13 (not_13_out, D0_q);
  not not_14 (not_14_out, x0);
  not not_15 (not_15_out, D2_q);
  not not_16 (not_16_out, D1_q);
  not not_17 (not_17_out, D2_q);
  not not_18 (not_18_out, D0_q);
  not not_19 (not_19_out, x2);
  not not_20 (not_20_out, x1);
  not not_21 (not_21_out, D1_q);
  not not_22 (not_22_out, D0_q);
  not not_23 (not_23_out, x0);
  not not_24 (not_24_out, D1_q);
  not not_25 (not_25_out, x2);
  not not_26 (not_26_out, x2);
  not not_27 (not_27_out, x1);
  not not_28 (not_28_out, x0);
  not not_29 (not_29_out, D1_q);
  not not_30 (not_30_out, D0_q);
  not not_31 (not_31_out, x0);
  not not_32 (not_32_out, D1_q);
  not not_33 (not_33_out, x2);
  not not_34 (not_34_out, x0);
  not not_35 (not_35_out, x0);
  not not_36 (not_36_out, x2);
  not not_37 (not_37_out, x1);
  not not_38 (not_38_out, x0);
  not not_39 (not_39_out, D2_q);
  not not_40 (not_40_out, D1_q);
  not not_41 (not_41_out, x0);
  not not_42 (not_42_out, D1_q);
  not not_43 (not_43_out, D0_q);
  not not_44 (not_44_out, x0);
  not not_45 (not_45_out, D1_q);
  and and_1 (and_1_out, not_1_out, not_2_out, D0_q);
  and and_2 (and_2_out, not_3_out, not_4_out, D1_q);
  and and_3 (and_3_out, not_5_out, x0, not_6_out, not_7_out, not_8_out);
  and and_4 (and_4_out, x1, not_9_out, not_10_out);
  and and_5 (and_5_out, x2, not_11_out, not_12_out, not_13_out);
  and and_6 (and_6_out, not_14_out, D1_q, D0_q);
  and and_7 (and_7_out, x2, x0, not_15_out, not_16_out);
  and and_8 (and_8_out, x2, x0, not_17_out, not_18_out);
  and and_9 (and_9_out, not_19_out, not_20_out, x0, D1_q);
  and and_10 (and_10_out, x1, x0, not_21_out, not_22_out);
  and and_11 (and_11_out, x2, not_23_out, not_24_out, D0_q);
  and and_12 (and_12_out, not_25_out, x0, D1_q, D0_q);
  and and_13 (and_13_out, not_26_out, not_27_out, x0, D1_q);
  and and_14 (and_14_out, x1, not_28_out, not_29_out, not_30_out);
  and and_15 (and_15_out, x2, not_31_out, not_32_out, D0_q);
  and and_16 (and_16_out, not_33_out, x0, D1_q, D0_q);
  and and_17 (and_17_out, not_34_out, D1_q);
  and and_18 (and_18_out, x1, not_35_out, D0_q);
  and and_19 (and_19_out, x2, D1_q);
  and and_20 (and_20_out, not_36_out, not_37_out, not_38_out, not_39_out, not_40_out);
  and and_21 (and_21_out, not_41_out, D1_q, D0_q);
  and and_22 (and_22_out, x1, x0, not_42_out, D0_q);
  and and_23 (and_23_out, x1, x0, D1_q, not_43_out);
  and and_24 (and_24_out, x2, not_44_out, D1_q);
  and and_25 (and_25_out, x2, x0, not_45_out, D0_q);
  or or_1 (y1, and_1_out, and_2_out, and_3_out, and_4_out, and_5_out, and_6_out, and_7_out, and_8_out);
  or or_2 (y0, D2_q, and_9_out, and_10_out, and_11_out, and_12_out);
  or or_3 (or_3_out, D2_q, and_13_out, and_14_out, and_15_out, and_16_out);
  or or_4 (or_4_out, and_17_out, and_18_out, and_19_out);
  or or_5 (or_5_out, and_20_out, and_21_out, and_22_out, and_23_out, and_24_out, and_25_out);
  D_Flip_Flop D2 (.clk(in_4), .D(or_3_out), .Q(D2_q));  // open: Qn, preset, en, reset
  D_Flip_Flop D1 (.clk(in_4), .D(or_4_out), .Q(D1_q));  // open: Qn, preset, en, reset
  D_Flip_Flop D0 (.clk(in_4), .D(or_5_out), .Q(D0_q));  // open: Qn, preset, en, reset

  // Notes on the sheet:
  //   Возможные действия:
  //   000 - завести автомобиль
  //   001 - заглушить автомобиль
  //   010 - опустить ручник
  //   011 - поднять ручник
  //   100 - тронуться
  //   101 - затормозить
  //   Состояния:
  //   Результат:
  //   00 - успешно
  //   01 - ошибка
  //   10 - ничего сделано
  //   011 - в состоянии движения
  //   100 - в нестабильном состоянии
  //   000 - в состоянии покоя, заглушена и на ручнике
  //   001 - в состоянии покоя, заведена и на ручнике
  //   010 - в состоянии покоя, заведена и снята с ручника
endmodule
